# Fritzing sketch layout (saved by Fritzing 0.9.3b)
breadboards: 1

parts:
  Part1 = Arduino Uno (Rev3) - ICSP
  R1 = Resistor [tolerance=±1% resistance=10k package=THT]
  R2 = Resistor [tolerance=±1% resistance=10k package=THT]
  R3 = Resistor [tolerance=±1% resistance=10k package=THT]
  R4 = Resistor [tolerance=±1% resistance=10k package=THT]
  R5 = Resistor [tolerance=±1% resistance=10k package=THT]
  R6 = Resistor [tolerance=±1% resistance=10k package=THT]
  R7 = Resistor [tolerance=±1% resistance=10k package=THT]
  R8 = Resistor [tolerance=±1% resistance=20k package=THT]
  R9 = Resistor [tolerance=±1% resistance=20k package=THT]
  R10 = Resistor [tolerance=±1% resistance=20k package=THT]
  R11 = Resistor [tolerance=±1% resistance=20k package=THT]
  R12 = Resistor [tolerance=±1% resistance=20k package=THT]
  R13 = Resistor [tolerance=±1% resistance=20k package=THT]
  R14 = Resistor [tolerance=±1% resistance=20k package=THT]
  R15 = Resistor [tolerance=±1% resistance=20k package=THT]
  R16 = Resistor [tolerance=±5% resistance=20k package=THT]
  SP1 = SPEAKER [package=pcb_mount_speaker]
  R17 = Rotary Potentiometer (Small) [maximum_resistance=10kΩ package=THT]
  U1 = LM386 [package=dip08]
  BAT1 = BC9VPC [package=bc9vpc]
  C1 = Electrolytic Capacitor [capacitance=220µF voltage=16V package="0605 [SMD, electrolytic]"]
  C3 = Electrolytic Capacitor [capacitance=220µF voltage=16V package="0605 [SMD, electrolytic]"]
  C4 = Capacitor Polarized [package=cpol-radial-1000uf-25v]

nets:
  N1: Part1.GND, R9.Pin_0, SP1.+, R17.leg1, U1.-IN, U1.V-, BAT1.V-, C1.-, C3.-
  N2: Part1.D0/RX, R16.Pin_1
  N3: Part1.D1/TX, R15.Pin_1
  N4: Part1.D2, R14.Pin_1
  N5: Part1.D3_PWM, R13.Pin_1
  N6: Part1.D4, R12.Pin_1
  N7: Part1.D5_PWM, R11.Pin_1
  N8: Part1.D6_PWM, R10.Pin_1
  N9: Part1.D7, R8.Pin_1
  N10: R1.Pin_0, R8.Pin_0, R17.leg2
  N11: R1.Pin_1, R2.Pin_0, R10.Pin_0
  N12: R2.Pin_1, R3.Pin_0, R11.Pin_0
  N13: R3.Pin_1, R4.Pin_0, R12.Pin_0
  N14: R4.Pin_1, R5.Pin_0, R13.Pin_0
  N15: R5.Pin_1, R6.Pin_0, R14.Pin_0
  N16: R6.Pin_1, R7.Pin_0, R15.Pin_0
  N17: R7.Pin_1, R9.Pin_1, R16.Pin_0
  N18: SP1.-, C4.-
  N19: R17.wiper, U1.+IN
  N20: U1.V+, BAT1.V+, C1.+
  N21: U1.BP, C3.+
