# Fritzing sketch layout (saved by Fritzing 0.9.3b)
breadboards: 3

parts:
  Part1 = Arduino Uno (Rev3) - ICSP
  hc-sr1 = hc-sr04
  R1 = Resistor [tolerance=±5% resistance=82 package="2512 [SMD]"]
  U1 = 74HC595 [package="DIP16 [THT]"]
  R2 = Resistor [tolerance=±5% resistance=82 package="2512 [SMD]"]
  R3 = Resistor [tolerance=±5% resistance=82 package="2512 [SMD]"]
  R4 = Resistor [tolerance=±5% resistance=82 package="2512 [SMD]"]
  R5 = Resistor [tolerance=±5% resistance=82 package="2512 [SMD]"]
  R6 = Resistor [tolerance=±5% resistance=82 package="2512 [SMD]"]
  R7 = Resistor [tolerance=±5% resistance=82 package="2512 [SMD]"]
  R8 = Resistor [tolerance=±5% resistance=82 package="2512 [SMD]"]
  LED1 = LED - 3mm [color="Blue (430nm)" package="3 mm [THT]"]
  LED2 = LED - 3mm [color="Blue (430nm)" package="3 mm [THT]"]
  LED3 = LED - 3mm [color="Blue (430nm)" package="3 mm [THT]"]
  LED4 = LED - 3mm [color="Blue (430nm)" package="3 mm [THT]"]
  LED5 = LED - 3mm [color="Blue (430nm)" package="3 mm [THT]"]
  LED6 = LED - 3mm [color="Blue (430nm)" package="3 mm [THT]"]
  LED7 = LED - 3mm [color="Blue (430nm)" package="3 mm [THT]"]
  LED8 = LED - 3mm [color="Blue (430nm)" package="3 mm [THT]"]
  R9 = Resistor [tolerance=±5% resistance=82 package="2512 [SMD]"]
  LED9 = LED - 3mm [color="Red (635nm)" package="3 mm [THT]"]
  R10 = Resistor [tolerance=±5% resistance=82 package="2512 [SMD]"]
  LED10 = LED - 3mm [color="Blue (430nm)" package="3 mm [THT]"]

nets:
  N1: Part1.ICSP_MOSI, Part1.D11_PWM/MOSI, U1.DS
  N2: Part1.D8, hc-sr1.Echo
  N3: Part1.D9_PWM, R9.Pin_0
  N4: Part1.D10_PWM/SS, U1.ST_CP
  N5: Part1.D13/SCK, U1.SH_CP
  GND: Part1.GND, hc-sr1.GND, LED1.anode, LED2.anode, LED3.anode, LED4.anode, LED5.anode, LED6.anode, LED7.anode, LED8.anode, LED9.anode, LED10.anode
  N6: Part1.D3_PWM, R10.Pin_0
  N7: Part1.D6_PWM, hc-sr1.Trig
  N8: Part1.D7, U1.OE
  VCC: Part1.5V, hc-sr1.VCC, U1.MR, U1.VCC
  N9: R1.Pin_0, U1.Q0
  N10: R1.Pin_1, LED8.cathode
  N11: U1.Q1, R2.Pin_0
  N12: U1.Q2, R3.Pin_0
  N13: U1.Q3, R4.Pin_0
  N14: U1.Q4, R5.Pin_0
  N15: U1.Q5, R6.Pin_0
  N16: U1.Q6, R7.Pin_0
  N17: U1.Q7, R8.Pin_0
  N18: R2.Pin_1, LED7.cathode
  N19: R3.Pin_1, LED6.cathode
  N20: R4.Pin_1, LED5.cathode
  N21: R5.Pin_1, LED4.cathode
  N22: R6.Pin_1, LED3.cathode
  N23: R7.Pin_1, LED2.cathode
  N24: R8.Pin_1, LED1.cathode
  N25: R9.Pin_1, LED9.cathode
  N26: R10.Pin_1, LED10.cathode
