# Fritzing sketch layout (saved by Fritzing 0.9.3b)
breadboards: 2

parts:
  Part1 = Arduino Uno (Rev3) - ICSP
  R1 = Resistor [tolerance=±5% resistance=20k package="0805 [SMD]"]
  R4 = Resistor [tolerance=±5% resistance=10k package="0805 [SMD]"]
  R5 = Resistor [tolerance=±5% resistance=10k package="0805 [SMD]"]
  R7 = Resistor [tolerance=±5% resistance=20k package="0805 [SMD]"]
  R9 = Resistor [tolerance=±5% resistance=20k package="0805 [SMD]"]
  R10 = Resistor [tolerance=±5% resistance=20k package="0805 [SMD]"]
  R11 = Resistor [tolerance=±5% resistance=20k package="0805 [SMD]"]
  R13 = Resistor [tolerance=±5% resistance=20k package="0805 [SMD]"]
  R14 = Resistor [tolerance=±5% resistance=20k package="0805 [SMD]"]
  LED1 = LED - 5mm [color="Red (633nm)" package="5 mm [THT]"]
  Part2 = MicroSD Card Module
  BAT1 = BC9VPC [package=bc9vpc]
  SP1 = SPEAKER [package=pcb_mount_speaker]
  U1 = LM386 [package=dip08]
  R17 = Rotary Potentiometer (Small) [maximum_resistance=10kΩ package=THT]
  C1 = Ceramic Capacitor [capacitance=50nF package="200 mil [THT, multilayer]"]
  R18 = Resistor [tolerance=±5% resistance=10 package="0805 [SMD]"]
  C4 = Electrolytic Capacitor [capacitance=470nF voltage=16V package="100 mil [THT, electrolytic]"]
  R20 = Resistor [tolerance=±5% resistance=10k package="0805 [SMD]"]
  R22 = Resistor [tolerance=±5% resistance=10k package="0805 [SMD]"]
  R25 = Resistor [tolerance=±5% resistance=20k package="0805 [SMD]"]
  R26 = Resistor [tolerance=±5% resistance=10k package="0805 [SMD]"]
  R27 = Resistor [tolerance=±5% resistance=20k package="0805 [SMD]"]
  R28 = Resistor [tolerance=±5% resistance=10k package="0805 [SMD]"]
  R29 = Resistor [tolerance=±5% resistance=10k package="0805 [SMD]"]

nets:
  N1: Part1.ICSP_MISO, Part1.D12/MISO, Part2.MISO
  N2: Part1.ICSP_MOSI, Part1.D11_PWM/MOSI, Part2.MOSI
  GND: Part1.GND, R1.Pin_1, LED1.cathode, Part2.GND, BAT1.V-, SP1.+, U1.-IN, U1.V-, R17.leg2, R18.Pin_1
  5V: Part1.5V, Part2.VCC
  N3: Part1.D9_PWM, LED1.anode
  N4: Part1.D10_PWM/SS, Part2.CS
  N5: Part1.D13/SCK, Part2.SCK
  N6: Part1.D0/RX, R7.Pin_0
  N7: Part1.D1/TX, R27.Pin_0
  N8: Part1.D2, R9.Pin_0
  N9: Part1.D3_PWM, R10.Pin_0
  N10: Part1.D4, R11.Pin_0
  N11: Part1.D5_PWM, R25.Pin_0
  N12: Part1.D6_PWM, R13.Pin_0
  N13: Part1.D7, R14.Pin_0
  N14: R1.Pin_0, R7.Pin_1, R22.Pin_0
  N15: R4.Pin_0, R9.Pin_1, R29.Pin_1
  N16: R4.Pin_1, R5.Pin_0, R10.Pin_1
  N17: R5.Pin_1, R11.Pin_1, R28.Pin_0
  N18: R13.Pin_1, R20.Pin_0, R26.Pin_1
  N19: R14.Pin_1, R17.leg1, R20.Pin_1
  N20: BAT1.V+, U1.V+, U1.BP
  N21: SP1.-, C4.-
  N22: U1.+IN, R17.wiper
  N23: U1.OUT, C1.0, C4.+
  N24: C1.1, R18.Pin_0
  N25: R22.Pin_1, R27.Pin_1, R29.Pin_0
  N26: R25.Pin_1, R26.Pin_0, R28.Pin_1
